# Fritzing sketch L02_00_Resistors Combined (saved by Fritzing 1.0.4)
breadboards: 1

parts:
  A1 = Particle - Photon2
  R1 = Resistor [tolerance=±5% power=0.25W resistance=5.1k package=THT]
  R2 = Resistor [tolerance=±5% power=0.25W resistance=5.1k package=THT]
  R3 = Resistor [tolerance=±5% power=0.25W resistance=1.2k package=THT]

nets (from the breadboard view):
  N1: A1.Pin_2, A1.Pin_31, R1.Pin_0, R2.Pin_0
  N2: A1.Pin_4, A1.Pin_30, R3.Pin_1
  N3: R1.Pin_1, R2.Pin_1, R3.Pin_0

custom parts:
  Particle - Photon2: The Photon 2 is a microcontroller and Wi-Fi networking developed by particle. Features: 802.11a/b/g/n Wi-Fi, 2.4 GHz and 5 GHz Integrated PCB antenna Integrated U.FL connector for external antenna Integrated RF switch BLE 5 using same antenna as Wi-Fi Realtek RTL8721DM MCU ARM Cortex M33 CPU, 200 MHz 2048 KB (2 MB) user application maximum size 3072 KB (3 MB) of RAM available to user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
